// Logisim project Oppgave1.circ as structural Verilog
module Counter (
  input  C_inn,
  input  Enable,
  input  Reset,
  output C_out,
  output [3:0] out_5
);

  wire clock_1_out;
  wire [3:0] adder_1_out;

  Register #(.width(4)) register_1 (.D(adder_1_out), .en(Enable), .Q(out_5), .clk(clock_1_out), .clr(Reset));
  Clock clock_1 (.out(clock_1_out));
  Adder #(.width(4)) adder_1 (.a(out_5), .b(4'b0001), .out(adder_1_out), .cin(C_inn), .cout(C_out));
endmodule

module StopAt15 (
);

  wire and_1_out, counter_2_c_out, not_1_out, not_2_out;
  wire [3:0] counter_1_out_5, counter_2_out_5;

  not not_1 (not_1_out, and_1_out);
  Counter counter_1 (.Enable(not_1_out), .C_inn(1'b0), .out_5(counter_1_out_5));  // open: Reset, C_out
  // Probe on counter_1_out_5
  and and_1 (and_1_out, counter_1_out_5[3], counter_1_out_5[2], counter_1_out_5[1], counter_1_out_5[0]);
  not not_2 (not_2_out, counter_2_c_out);
  Counter counter_2 (.Enable(not_2_out), .out_5(counter_2_out_5), .C_out(counter_2_c_out));  // open: C_inn, Reset
  // Probe on counter_2_out_5
endmodule
