// Logisim project Oppgave3.circ as structural Verilog
module RAM (
  input  [3:0] Address,
  input  [3:0] in_2,
  input  Select,
  input  Clear,
  input  Load,
  output [3:0] out_6
);

  wire not_1_out;
  wire [3:0] ram_1_data;

  RAM_part #(.addrWidth(4), .dataWidth(4), .bus("asynch")) ram_1 (
    .addr(Address), .data(ram_1_data), .sel(Select), .ld(Load), .clr(Clear));
  assign ram_1_data = not_1_out ? in_2 : 4'bz;  // Controlled_Buffer controlled_buffer_1
  assign out_6 = Load ? ram_1_data : 4'bz;  // Controlled_Buffer controlled_buffer_2
  not not_1 (not_1_out, Load);
endmodule

module LetThrough4bit (
  input  [3:0] in_1,
  input  in_2,
  input  in_3,
  input  in_4,
  input  in_5,
  output [3:0] out_6,
  output out_7,
  output out_8
);

  wire transistor_1_out;

  and and_1 (out_6[0], in_3, in_1[0]);
  and and_2 (out_6[1], in_3, in_1[1]);
  and and_3 (out_6[2], in_3, in_1[2]);
  and and_4 (out_6[3], in_3, in_1[3]);
  Transistor #(.\type ("n")) transistor_1 (.in(1'b1), .out(transistor_1_out), .gate(in_4));
  Transistor #(.\type ("n")) transistor_2 (.in(transistor_1_out), .out(out_8), .gate(in_5));
  Transistor transistor_3 (.in(1'b0), .out(out_8), .gate(in_5));
  Transistor #(.gate("br")) transistor_4 (.in(1'b0), .out(out_8), .gate(in_4));
  Transistor transistor_5 (.in(1'b1), .out(out_7), .gate(in_2));
  Transistor #(.\type ("n")) transistor_6 (.in(1'b0), .out(out_7), .gate(in_2));
endmodule
